# Fritzing sketch HC-SR04 (saved by Fritzing 0.9.1b)
breadboards: 1

parts:
  Part1 = SRF05 Ultrasonic Rangefinder
  Part2 = Arduino Uno (Rev3)

nets:
  VCC: Part1.VCC, Part2.5V
  N1: Part1.Trig, Part2.D12/MISO
  N2: Part1.Echo, Part2.D11_PWM/MOSI
  GND: Part1.GND, Part2.GND
